// Logisim project Project Pt.5.circ as structural Verilog: 12 circuits, main circuit CPU
module CPU (
  input  [31:0] DataFromBus,
  output BusWriteEnable,
  output [15:0] AddressToBus,
  output [31:0] DataToBus
);

  wire alu_1_equal, and_1_out, and_2_out, clock_1_out, control_1_beqselect, control_1_bneselect,
       control_1_immselect, control_1_jalr, control_1_jalselect, control_1_jrselect, control_1_jselect,
       control_1_lwselect, control_1_reg_write_e, control_1_shiftslect, or_1_out, or_2_out, or_3_out,
       or_4_out;
  wire [3:0] control_1_alu_select;
  wire [4:0] control_1_rd, control_1_rs, control_1_rt;
  wire [15:0] bit_extender_2_out;
  wire [25:0] bit_extender_3_out, shifter_2_out;
  wire [31:0] adder_1_out, adder_2_out, adder_3_out, alu_1_out_4, bit_extender_1_out, control_1_imm,
       control_1_sa, multiplexer_1_out, multiplexer_2_out, multiplexer_3_out, multiplexer_4_out,
       multiplexer_5_out, multiplexer_6_out, multiplexer_7_out, ProgramCounter_q, regfile_1_rs_data,
       rom_1_data, shifter_1_out, shifter_3_out;

  Adder #(.width(32)) adder_1 (.a(ProgramCounter_q), .b(32'h4), .out(adder_1_out));  // open: cin, cout
  Shifter #(.width(32)) shifter_1 (.in(control_1_imm), .\dist (5'b00010), .out(shifter_1_out));
  Adder #(.width(32)) adder_2 (.a(adder_1_out), .b(shifter_1_out), .out(adder_2_out));  // open: cin, cout
  Shifter #(.width(26)) shifter_2 (.in(bit_extender_3_out), .\dist (5'b00010), .out(shifter_2_out));
  Multiplexer #(.width(32)) multiplexer_1 (
    .in0(adder_1_out), .in1(adder_2_out), .out(multiplexer_1_out), .sel(or_4_out));
  assign bit_extender_1_out = {{6{shifter_2_out[25]}}, shifter_2_out};  // Bit_Extender bit_extender_1
  Multiplexer #(.width(32)) multiplexer_2 (
    .in0(bit_extender_1_out), .in1(adder_3_out), .out(multiplexer_2_out), .sel(or_2_out));
  Multiplexer #(.width(32)) multiplexer_3 (
    .in0(multiplexer_1_out), .in1(multiplexer_2_out), .out(multiplexer_3_out), .sel(or_1_out));
  Adder #(.width(32)) adder_3 (.a(regfile_1_rs_data), .b(32'h2), .out(adder_3_out));  // open: cin, cout
  or or_1 (or_1_out, or_2_out, control_1_jselect, or_3_out);
  Register #(.width(32)) ProgramCounter (
    .D(multiplexer_3_out), .en(1'b1), .clk(clock_1_out), .Q(ProgramCounter_q));  // open: clr
  Clock clock_1 (.out(clock_1_out));
  Shifter #(.shift("lr"), .width(32)) shifter_3 (.in(ProgramCounter_q), .\dist (5'b00010), .out(shifter_3_out));
  ROM #(.addrWidth(16), .dataWidth(32)) rom_1 (.addr(bit_extender_2_out), .data(rom_1_data));
  Bit_Extender #(.in_width(32)) bit_extender_2 (.in(shifter_3_out), .out(bit_extender_2_out));
  // Probe on nothing
  Bit_Extender #(.in_width(32), .out_width(26)) bit_extender_3 (.in(rom_1_data), .out(bit_extender_3_out));
  Multiplexer #(.width(32)) multiplexer_4 (
    .in0(alu_1_out_4), .in1(DataFromBus), .out(multiplexer_4_out), .sel(control_1_lwselect));
  or or_2 (or_2_out, control_1_jrselect, control_1_jalr);
  or or_3 (or_3_out, control_1_jalr, control_1_jalselect);
  Multiplexer #(.width(32)) multiplexer_5 (
    .in0(multiplexer_4_out), .in1(adder_1_out), .out(multiplexer_5_out), .sel(or_3_out));
  or or_4 (or_4_out, and_1_out, and_2_out);
  Control control_1 (
    .Inst(rom_1_data), .lwSelect(control_1_lwselect), .swSelect(BusWriteEnable),
    .beqSelect(control_1_beqselect), .bneSelect(control_1_bneselect), .jSelect(control_1_jselect),
    .jalSelect(control_1_jalselect), .immSelect(control_1_immselect), .SA(control_1_sa), .imm(control_1_imm),
    .rs(control_1_rs), .rt(control_1_rt), .rd(control_1_rd), .reg_write_e(control_1_reg_write_e),
    .shiftSlect(control_1_shiftslect), .ALU_Select(control_1_alu_select), .jrSelect(control_1_jrselect),
    .jalr(control_1_jalr));
  // Probe on DataToBus
  regfile regfile_1 (
    .rd(control_1_rd), .rt(control_1_rt), .rs(control_1_rs), .write_e(control_1_reg_write_e),
    .rd_data(multiplexer_5_out), .rt_data(DataToBus), .rs_data(regfile_1_rs_data));
  and and_1 (and_1_out, alu_1_equal, control_1_bneselect);
  and and_2 (and_2_out, alu_1_equal, control_1_beqselect);
  Multiplexer #(.width(32)) multiplexer_6 (
    .in0(regfile_1_rs_data), .in1(control_1_sa), .out(multiplexer_6_out), .sel(control_1_shiftslect));
  Multiplexer #(.width(32)) multiplexer_7 (
    .in0(DataToBus), .in1(control_1_imm), .out(multiplexer_7_out), .sel(control_1_immselect));
  // Probe on DataFromBus
  // Probe on multiplexer_6_out
  // Probe on multiplexer_7_out
  // Probe on alu_1_out_4
  ALU alu_1 (
    .Control(control_1_alu_select), .OP1(multiplexer_6_out), .OP2(multiplexer_7_out), .out_4(alu_1_out_4),
    .Equal(alu_1_equal));
  // Probe on alu_1_out_4
  Bit_Extender #(.in_width(32)) bit_extender_4 (.in(alu_1_out_4), .out(AddressToBus));

  // Notes on the sheet:
  //   offset: (word addressed)
  //   PC + 4
  //   PC + 4 + Offset
  //   label: for j, jal (word addressed)
  //   if branch is to be taken
  //   register: for jr, jalr (byte addressed)
  //   jr/jalr
  //   any j*
  //   1 if two registers are ==
  //   contents of rom_1 (hex, n*v repeats v):
  //   14400002 201dff7c 8000071 201b0005 105b0016 201b0009 105b0050 201b000a 105b000a 201b000c 105b000a
  //   201b0041 105b005e 201b0042 105b0060 201b0045 105b004f 201b0050 105b0048 8000013 3400008 8c1bff80
  //   13600002 8c02ff84 800001a 20020000 3400008 23bdfffc afa80000 20030000 23bdfffc afba0000 2002000c
  //   d00c 8fba0000 23bd0004 1040fff9 20080020 1048002c 10600003 201b000a 7b0018 1812 201b0030 145b0002
  //   20630000 8000052 237b0001 145b0002 20630001 8000052 237b0001 145b0002 20630002 8000052 237b0001
  //   145b0002 20630003 8000052 237b0001 145b0002 20630004 8000052 237b0001 145b0002 20630005 8000052
  //   237b0001 145b0002 20630006 8000052 237b0001 145b0002 20630007 8000052 237b0001 145b0002 20630008
  //   8000052 237b0001 145b0002 20630009 800001e 20620000 8fa80000 23bd0004 3400008 8c9b0000 365d820
  //   ac9b0000 3400008 ac04ff90 ac05ff94 ac06ff98 ac00ff9c 3400008 23bdfff8 afa80000 afa90004 8c08ffac
  //   8c09ffb0 81020 91820 8fa80000 8fa90004 23bd0008 3400008 ac04ffa4 ac05ffa8 ac06ffac 3400008 ac04ffa0
  //   3400008 23bdffd0 200800ff 84a00 85400 200b007f b6200 b6c00 afaa0000 14cc020 afb80004 149c020
  //   afb80008 1a9c020 afb8000c afa90010 169c020 afb80014 109c020 afb80018 10cc020 afb8001c afa80020
  //   10dc020 afb80024 10ac020 afb80028 16ac020 afb8002c 1dc820 23bdc100 3a09820 20090000 ac9b0000
  //   20100040 2011003f 20120000 20080064 2002000c d00c 10400045 404020 20140000 22020 20020042 d00c
  //   20090077 15090002 2231ffff 80000bd 20090061 15090002 2210ffff 80000bd 20090073 15090002 22310001
  //   80000bd 20090064 15090002 22100001 80000bd ac00ff80 22520001 200e000c 24e001a 9010 127080 1d97020
  //   8dce0000 2002020 2202820 1c03020 3820 20020050 d00c 8000096 200f0040 200582a 15600017 200f003f
  //   220582a 15600014 200f007e 1f0582a 15600011 200f0080 1f1602a 1580000e 200e0004 1d00018 4812 200e01f8
  //   1d10018 7012 1c97020 1d37020 8dc90000 15200004 20090001 adc90000 1680ffd9 80000ae 200401b8 20050001
  //   20060032 20020041 d00c 2002000a d00c 20140001 800009e
  //   immediate
  //   label to jump to
  //   rs-data
  //   probe to help test the value in a wire
  //   PC + 4
  //   ALU
  //   MEM
  //   jal/jalr
  //   value from memory
  //   value from ALU
endmodule

module regfile (
  input  write_e,
  input  [4:0] rd,
  input  [31:0] rd_data,
  input  [4:0] rs,
  input  [4:0] rt,
  output [31:0] rs_data,
  output [31:0] rt_data
);

  wire clock_1_out, demultiplexer_1_out0, demultiplexer_1_out1, demultiplexer_1_out2, demultiplexer_1_out3,
       demultiplexer_1_out4, demultiplexer_1_out5, demultiplexer_1_out6, demultiplexer_1_out7,
       demultiplexer_1_out8, demultiplexer_1_out9, demultiplexer_1_out10, demultiplexer_1_out11,
       demultiplexer_1_out12, demultiplexer_1_out13, demultiplexer_1_out14, demultiplexer_1_out15,
       demultiplexer_1_out16, demultiplexer_1_out17, demultiplexer_1_out18, demultiplexer_1_out19,
       demultiplexer_1_out20, demultiplexer_1_out21, demultiplexer_1_out22, demultiplexer_1_out23,
       demultiplexer_1_out24, demultiplexer_1_out25, demultiplexer_1_out26, demultiplexer_1_out27,
       demultiplexer_1_out28, demultiplexer_1_out29, demultiplexer_1_out30, demultiplexer_1_out31;
  wire [31:0] R0_q, R1_q, R2_q, R3_q, R4_q, R5_q, R6_q, R7_q, R8_q, R9_q, R10_q, R11_q, R12_q, R13_q, R14_q,
       R15_q, R16_q, R17_q, R18_q, R19_q, R20_q, R21_q, R22_q, R23_q, R24_q, R25_q, R26_q, R27_q, R28_q,
       R29_q, R30_q, R31_q;

  Clock clock_1 (.out(clock_1_out));
  Register #(.width(32)) R8 (.D(rd_data), .en(demultiplexer_1_out8), .clk(clock_1_out), .Q(R8_q));  // open: clr
  Register #(.width(32)) R0 (.D({32{1'b0}}), .en(demultiplexer_1_out0), .clk(clock_1_out), .Q(R0_q));  // open: clr
  // Probe on R8_q
  Register #(.width(32)) R9 (.D(rd_data), .en(demultiplexer_1_out9), .clk(clock_1_out), .Q(R9_q));  // open: clr
  Register #(.width(32)) R1 (.D(rd_data), .en(demultiplexer_1_out1), .clk(clock_1_out), .Q(R1_q));  // open: clr
  // Probe on R9_q
  Register #(.width(32)) R10 (.D(rd_data), .en(demultiplexer_1_out10), .clk(clock_1_out), .Q(R10_q));  // open: clr
  Register #(.width(32)) R2 (.D(rd_data), .en(demultiplexer_1_out2), .clk(clock_1_out), .Q(R2_q));  // open: clr
  // Probe on R10_q
  Register #(.width(32)) R11 (.D(rd_data), .en(demultiplexer_1_out11), .clk(clock_1_out), .Q(R11_q));  // open: clr
  Register #(.width(32)) R3 (.D(rd_data), .en(demultiplexer_1_out3), .clk(clock_1_out), .Q(R3_q));  // open: clr
  // Probe on R11_q
  Register #(.width(32)) R12 (.D(rd_data), .en(demultiplexer_1_out12), .clk(clock_1_out), .Q(R12_q));  // open: clr
  Register #(.width(32)) R4 (.D(rd_data), .en(demultiplexer_1_out4), .clk(clock_1_out), .Q(R4_q));  // open: clr
  Demultiplexer #(.select(5)) demultiplexer_1 (
    .out0(demultiplexer_1_out0), .out1(demultiplexer_1_out1), .out2(demultiplexer_1_out2),
    .out3(demultiplexer_1_out3), .out4(demultiplexer_1_out4), .out5(demultiplexer_1_out5),
    .out6(demultiplexer_1_out6), .out7(demultiplexer_1_out7), .out8(demultiplexer_1_out8),
    .out9(demultiplexer_1_out9), .out10(demultiplexer_1_out10), .out11(demultiplexer_1_out11),
    .out12(demultiplexer_1_out12), .out13(demultiplexer_1_out13), .out14(demultiplexer_1_out14),
    .out15(demultiplexer_1_out15), .out16(demultiplexer_1_out16), .out17(demultiplexer_1_out17),
    .out18(demultiplexer_1_out18), .out19(demultiplexer_1_out19), .out20(demultiplexer_1_out20),
    .out21(demultiplexer_1_out21), .out22(demultiplexer_1_out22), .out23(demultiplexer_1_out23),
    .out24(demultiplexer_1_out24), .out25(demultiplexer_1_out25), .out26(demultiplexer_1_out26),
    .out27(demultiplexer_1_out27), .out28(demultiplexer_1_out28), .out29(demultiplexer_1_out29),
    .out30(demultiplexer_1_out30), .out31(demultiplexer_1_out31), .in(write_e), .sel(rd));
  // Probe on R12_q
  Register #(.width(32)) R13 (.D(rd_data), .en(demultiplexer_1_out13), .clk(clock_1_out), .Q(R13_q));  // open: clr
  Register #(.width(32)) R5 (.D(rd_data), .en(demultiplexer_1_out5), .clk(clock_1_out), .Q(R5_q));  // open: clr
  // Probe on R13_q
  Multiplexer #(.select(5), .width(32)) multiplexer_1 (
    .in0(R0_q), .in1(R1_q), .in2(R2_q), .in3(R3_q), .in4(R4_q), .in5(R5_q), .in6(R6_q), .in7(R7_q),
    .in8(R8_q), .in9(R9_q), .in10(R10_q), .in11(R11_q), .in12(R12_q), .in13(R13_q), .in14(R14_q),
    .in15(R15_q), .in16(R16_q), .in17(R17_q), .in18(R18_q), .in19(R19_q), .in20(R20_q), .in21(R21_q),
    .in22(R22_q), .in23(R23_q), .in24(R24_q), .in25(R25_q), .in26(R26_q), .in27(R27_q), .in28(R28_q),
    .in29(R29_q), .in30(R30_q), .in31(R31_q), .out(rs_data), .sel(rs));
  Multiplexer #(.select(5), .width(32)) multiplexer_2 (
    .in0(R0_q), .in1(R1_q), .in2(R2_q), .in3(R3_q), .in4(R4_q), .in5(R5_q), .in6(R6_q), .in7(R7_q),
    .in8(R8_q), .in9(R9_q), .in10(R10_q), .in11(R11_q), .in12(R12_q), .in13(R13_q), .in14(R14_q),
    .in15(R15_q), .in16(R16_q), .in17(R17_q), .in18(R18_q), .in19(R19_q), .in20(R20_q), .in21(R21_q),
    .in22(R22_q), .in23(R23_q), .in24(R24_q), .in25(R25_q), .in26(R26_q), .in27(R27_q), .in28(R28_q),
    .in29(R29_q), .in30(R30_q), .in31(R31_q), .out(rt_data), .sel(rt));
  Register #(.width(32)) R14 (.D(rd_data), .en(demultiplexer_1_out14), .clk(clock_1_out), .Q(R14_q));  // open: clr
  Register #(.width(32)) R6 (.D(rd_data), .en(demultiplexer_1_out6), .clk(clock_1_out), .Q(R6_q));  // open: clr
  Register #(.width(32)) R15 (.D(rd_data), .en(demultiplexer_1_out15), .clk(clock_1_out), .Q(R15_q));  // open: clr
  Register #(.width(32)) R7 (.D(rd_data), .en(demultiplexer_1_out7), .clk(clock_1_out), .Q(R7_q));  // open: clr
  Register #(.width(32)) R16 (.D(rd_data), .en(demultiplexer_1_out16), .clk(clock_1_out), .Q(R16_q));  // open: clr
  Register #(.width(32)) R24 (.D(rd_data), .en(demultiplexer_1_out24), .clk(clock_1_out), .Q(R24_q));  // open: clr
  Register #(.width(32)) R17 (.D(rd_data), .en(demultiplexer_1_out17), .clk(clock_1_out), .Q(R17_q));  // open: clr
  Register #(.width(32)) R25 (.D(rd_data), .en(demultiplexer_1_out25), .clk(clock_1_out), .Q(R25_q));  // open: clr
  Register #(.width(32)) R18 (.D(rd_data), .en(demultiplexer_1_out18), .clk(clock_1_out), .Q(R18_q));  // open: clr
  Register #(.width(32)) R26 (.D(rd_data), .en(demultiplexer_1_out26), .clk(clock_1_out), .Q(R26_q));  // open: clr
  Register #(.width(32)) R19 (.D(rd_data), .en(demultiplexer_1_out19), .clk(clock_1_out), .Q(R19_q));  // open: clr
  Register #(.width(32)) R27 (.D(rd_data), .en(demultiplexer_1_out27), .clk(clock_1_out), .Q(R27_q));  // open: clr
  Register #(.width(32)) R20 (.D(rd_data), .en(demultiplexer_1_out20), .clk(clock_1_out), .Q(R20_q));  // open: clr
  Register #(.width(32)) R28 (.D(rd_data), .en(demultiplexer_1_out28), .clk(clock_1_out), .Q(R28_q));  // open: clr
  Register #(.width(32)) R21 (.D(rd_data), .en(demultiplexer_1_out21), .clk(clock_1_out), .Q(R21_q));  // open: clr
  Register #(.width(32)) R29 (.D(rd_data), .en(demultiplexer_1_out29), .clk(clock_1_out), .Q(R29_q));  // open: clr
  // Probe on R29_q
  Register #(.width(32)) R22 (.D(rd_data), .en(demultiplexer_1_out22), .clk(clock_1_out), .Q(R22_q));  // open: clr
  Register #(.width(32)) R30 (.D(rd_data), .en(demultiplexer_1_out30), .clk(clock_1_out), .Q(R30_q));  // open: clr
  Register #(.width(32)) R23 (.D(rd_data), .en(demultiplexer_1_out23), .clk(clock_1_out), .Q(R23_q));  // open: clr
  Register #(.width(32)) R31 (.D(rd_data), .en(demultiplexer_1_out31), .clk(clock_1_out), .Q(R31_q));  // open: clr
endmodule

module Control (
  input  [31:0] Inst,
  output lwSelect,
  output swSelect,
  output beqSelect,
  output bneSelect,
  output jSelect,
  output jalSelect,
  output immSelect,
  output [31:0] SA,
  output [31:0] imm,
  output [4:0] rs,
  output [4:0] rt,
  output [4:0] rd,
  output reg_write_e,
  output shiftSlect,
  output [3:0] ALU_Select,
  output jrSelect,
  output jalr
);

  wire comparator_7_eq, comparator_8_eq, comparator_9_eq, comparator_10_eq, comparator_11_eq,
       comparator_12_eq, comparator_13_eq, comparator_14_eq, comparator_15_eq, comparator_16_eq,
       comparator_17_eq, comparator_19_eq, comparator_20_eq, or_1_out, or_2_out, or_4_out, or_5_out,
       or_7_out, or_9_out, or_10_out;
  wire [4:0] multiplexer_2_out;
  wire [5:0] multiplexer_1_out;
  wire [31:0] adder_1_out, bit_extender_1_out, bit_extender_3_out, multiplexer_16_out;

  or or_1 (or_1_out, swSelect, beqSelect, bneSelect, jSelect);
  Comparator #(.width(6)) comparator_1 (.a(6'b100011), .b(Inst[31:26]), .eq(lwSelect));  // open: gt, lt
  Comparator #(.width(6)) comparator_2 (.a(6'b101011), .b(Inst[31:26]), .eq(swSelect));  // open: gt, lt
  Comparator #(.width(6)) comparator_3 (.a(6'b000100), .b(Inst[31:26]), .eq(beqSelect));  // open: gt, lt
  Comparator #(.width(6)) comparator_4 (.a(6'b000101), .b(Inst[31:26]), .eq(bneSelect));  // open: gt, lt
  Comparator #(.width(6)) comparator_5 (.a(6'b000010), .b(Inst[31:26]), .eq(jSelect));  // open: gt, lt
  Comparator #(.width(6)) comparator_6 (.a(6'b000011), .b(Inst[31:26]), .eq(jalSelect));  // open: gt, lt
  Comparator #(.width(6)) comparator_7 (.a({6{1'b0}}), .b(Inst[31:26]), .eq(comparator_7_eq));  // open: gt, lt
  Comparator #(.width(6)) comparator_8 (.a(6'b001000), .b(Inst[31:26]), .eq(comparator_8_eq));  // open: gt, lt
  Multiplexer #(.width(6)) multiplexer_1 (
    .in0({6{1'b1}}), .in1(Inst[5:0]), .out(multiplexer_1_out), .sel(comparator_7_eq));
  Comparator #(.width(6)) comparator_9 (.a(multiplexer_1_out), .b(6'b011010), .eq(comparator_9_eq));  // open: gt, lt
  Comparator #(.width(6)) comparator_10 (.a(multiplexer_1_out), .b(6'b011000), .eq(comparator_10_eq));  // open: gt, lt
  Comparator #(.width(6)) comparator_11 (.a(multiplexer_1_out), .b(6'b010010), .eq(comparator_11_eq));  // open: gt, lt
  Comparator #(.width(6)) comparator_12 (.a(multiplexer_1_out), .b(6'b010000), .eq(comparator_12_eq));  // open: gt, lt
  Comparator #(.width(6)) comparator_13 (.a(multiplexer_1_out), .b({6{1'b0}}), .eq(comparator_13_eq));  // open: gt, lt
  Comparator #(.width(6)) comparator_14 (.a(multiplexer_1_out), .b(6'b000010), .eq(comparator_14_eq));  // open: gt, lt
  Comparator #(.width(6)) comparator_15 (.a(multiplexer_1_out), .b(6'b100000), .eq(comparator_15_eq));  // open: gt, lt
  Comparator #(.width(6)) comparator_16 (.a(multiplexer_1_out), .b(6'b100010), .eq(comparator_16_eq));  // open: gt, lt
  Comparator #(.width(6)) comparator_17 (.a(multiplexer_1_out), .b(6'b101010), .eq(comparator_17_eq));  // open: gt, lt
  Comparator #(.width(6)) comparator_18 (.a(multiplexer_1_out), .b(6'b001000), .eq(jrSelect));  // open: gt, lt
  Comparator #(.width(6)) comparator_19 (.a(multiplexer_1_out), .b(6'b001001), .eq(comparator_19_eq));  // open: gt, lt
  Comparator #(.width(6)) comparator_20 (.a(multiplexer_1_out), .b(6'b001100), .eq(comparator_20_eq));  // open: gt, lt
  or or_2 (or_2_out, comparator_19_eq, comparator_20_eq);
  or or_3 (immSelect, jalSelect, swSelect, lwSelect, or_2_out, comparator_8_eq);
  or or_4 (or_4_out, lwSelect, comparator_8_eq);
  Multiplexer #(.width(5)) multiplexer_2 (
    .in0(Inst[15:11]), .in1(Inst[20:16]), .out(multiplexer_2_out), .sel(or_4_out));
  or or_5 (or_5_out, comparator_9_eq, or_1_out, jrSelect, comparator_10_eq);
  or or_6 (shiftSlect, comparator_13_eq, comparator_14_eq);
  or or_7 (or_7_out, jalSelect, comparator_19_eq);
  Multiplexer #(.width(5)) multiplexer_3 (.in0(multiplexer_2_out), .in1({5{1'b1}}), .out(rd), .sel(or_7_out));
  Multiplexer #(.width(4)) multiplexer_4 (.in1(4'b1110), .out(ALU_Select), .sel(beqSelect));  // open: in0
  Multiplexer #(.width(4)) multiplexer_5 (.in1(4'b1100), .out(ALU_Select), .sel(bneSelect));  // open: in0
  Multiplexer #(.width(4)) multiplexer_6 (.in1(4'b0000), .out(ALU_Select), .sel(comparator_8_eq));  // open: in0
  Multiplexer #(.width(4)) multiplexer_7 (.in1(4'b1001), .out(ALU_Select), .sel(comparator_9_eq));  // open: in0
  Multiplexer #(.width(4)) multiplexer_8 (.in1(4'b1000), .out(ALU_Select), .sel(comparator_10_eq));  // open: in0
  Multiplexer #(.width(4)) multiplexer_9 (.in1(4'b0100), .out(ALU_Select), .sel(comparator_11_eq));  // open: in0
  Multiplexer #(.width(4)) multiplexer_10 (.in1(4'b0101), .out(ALU_Select), .sel(comparator_12_eq));  // open: in0
  Multiplexer #(.width(4)) multiplexer_11 (.in1(4'b0010), .out(ALU_Select), .sel(comparator_13_eq));  // open: in0
  Multiplexer #(.width(4)) multiplexer_12 (.in1(4'b0011), .out(ALU_Select), .sel(comparator_14_eq));  // open: in0
  Multiplexer #(.width(4)) multiplexer_13 (.in1(4'b0000), .out(ALU_Select), .sel(comparator_15_eq));  // open: in0
  Multiplexer #(.width(4)) multiplexer_14 (.in1(4'b0001), .out(ALU_Select), .sel(comparator_16_eq));  // open: in0
  Multiplexer #(.width(4)) multiplexer_15 (.in1(4'b1111), .out(ALU_Select), .sel(comparator_17_eq));  // open: in0
  or or_8 (jalr, comparator_19_eq, comparator_20_eq);
  assign bit_extender_1_out = {{16{Inst[15]}}, Inst[15:0]};  // Bit_Extender bit_extender_1
  assign SA = {{27{Inst[10]}}, Inst[10:6]};  // Bit_Extender bit_extender_2
  or or_9 (or_9_out, lwSelect, swSelect);
  or or_10 (or_10_out, jSelect, jalSelect);
  not not_1 (reg_write_e, or_5_out);
  assign bit_extender_3_out = {{27{1'b0}}, Inst[25:21]};  // Bit_Extender bit_extender_3
  Multiplexer #(.width(32)) multiplexer_16 (
    .in0({32{1'b0}}), .in1(bit_extender_3_out), .out(multiplexer_16_out), .sel(or_9_out));
  Adder #(.width(32)) adder_1 (.a(multiplexer_16_out), .b(bit_extender_1_out), .out(adder_1_out));  // open: cin, cout
  Multiplexer #(.width(32)) multiplexer_17 (
    .in0(adder_1_out), .in1({{6{1'b0}}, Inst[25:0]}), .out(imm), .sel(or_10_out));

  assign rs = Inst[25:21];
  assign rt = Inst[20:16];

  // Notes on the sheet:
  //   split-key:
  //   offset
  //   base
  //   func
  //   other
  //   rd
  //   rt
  //   rs
  //   opcode
  //   func codes...
  //   lw
  //   sw
  //   beq
  //   bne
  //   j
  //   jal
  //   opcode 000000
  //   addi
  //   div
  //   mult
  //   mflo
  //   mfhi
  //   sll
  //   srl
  //   add
  //   sub
  //   slt
  //   jr
  //   jalr
  //   syscall
  //   reg write
  //   target
  //   rt as rd
  //   ra as rd
  //   ALU code determination
  //   offset
  //   FIX: rd as ra for jal and jalr   
  //   target
  //   imm/offset/target
endmodule

module ALU (
  input  [3:0] Control,
  input  [31:0] OP1,
  input  [31:0] OP2,
  output [31:0] out_4,
  output Equal
);

  wire clock_1_out, comparator_1_eq, comparator_1_gt, comparator_1_lt, comparator_2_eq, comparator_2_gt,
       comparator_2_lt, multiplexer_1_out, not_1_out, or_1_out, or_2_out;
  wire [4:0] bit_extender_1_out;
  wire [31:0] adder_1_out, divider_1_out, divider_1_rem, HI_q, LO_q, multiplexer_4_out, multiplexer_5_out,
       multiplexer_6_out, multiplexer_8_out, multiplexer_9_out, multiplexer_10_out, multiplexer_11_out,
       multiplexer_12_out, multiplexer_13_out, multiplexer_14_out, multiplexer_15_out, multiplexer_16_out,
       multiplexer_17_out, multiplier_1_cout, multiplier_1_out, shifter_1_out, shifter_2_out,
       subtractor_1_out;

  Comparator #(.width(32)) comparator_1 (
    .a(OP1), .b(OP2), .gt(comparator_1_gt), .eq(comparator_1_eq), .lt(comparator_1_lt));
  Bit_Extender #(.in_width(32), .out_width(5)) bit_extender_1 (.in(OP1), .out(bit_extender_1_out));
  Multiplexer multiplexer_1 (.in0(1'b0), .in1(1'b1), .out(multiplexer_1_out), .sel(comparator_1_eq));
  Comparator #(.width(32)) comparator_2 (
    .a(OP1), .b(OP2), .gt(comparator_2_gt), .eq(comparator_2_eq), .lt(comparator_2_lt));
  or or_1 (or_1_out, comparator_1_gt, comparator_1_lt);
  not not_1 (not_1_out, multiplexer_1_out);
  Adder #(.width(32)) adder_1 (.a(OP1), .b(OP2), .out(adder_1_out));  // open: cin, cout
  Subtractor #(.width(32)) subtractor_1 (.a(OP1), .b(OP2), .out(subtractor_1_out));  // open: bin, bout
  Shifter #(.width(32)) shifter_1 (.in(OP2), .\dist (bit_extender_1_out), .out(shifter_1_out));
  Shifter #(.shift("lr"), .width(32)) shifter_2 (.in(OP2), .\dist (bit_extender_1_out), .out(shifter_2_out));
  or or_2 (or_2_out, comparator_2_gt, comparator_2_eq);
  Multiplier #(.width(32)) multiplier_1 (
    .a(OP1), .b(OP2), .out(multiplier_1_out), .cout(multiplier_1_cout));  // open: cin
  Divider #(.width(32)) divider_1 (.a(OP1), .b(OP2), .out(divider_1_out), .rem(divider_1_rem));  // open: upper
  Multiplexer multiplexer_2 (.in1(1'b0), .out(multiplexer_1_out), .sel(or_1_out));  // open: in0
  Multiplexer #(.select(4)) multiplexer_3 (
    .in0(1'b0), .in1(1'b0), .in2(1'b0), .in3(1'b0), .in4(1'b0), .in5(1'b0), .in6(1'b0), .in7(1'b0),
    .in8(1'b0), .in9(1'b0), .in10(1'b0), .in11(1'b0), .in12(not_1_out), .in13(1'b0),
    .in14(multiplexer_1_out), .in15(1'b0), .out(Equal), .sel(Control));
  Multiplexer #(.width(32)) multiplexer_4 (
    .in0(adder_1_out), .in1(subtractor_1_out), .out(multiplexer_4_out), .sel(Control[0]));
  Multiplexer #(.width(32)) multiplexer_5 (
    .in0(shifter_1_out), .in1(shifter_2_out), .out(multiplexer_5_out), .sel(Control[0]));
  Multiplexer #(.width(32)) multiplexer_6 (.in1(32'h1), .out(multiplexer_6_out), .sel(comparator_2_lt));  // open: in0
  Multiplexer #(.width(32)) multiplexer_7 (.in1({32{1'b0}}), .out(multiplexer_6_out), .sel(or_2_out));  // open: in0
  Multiplexer #(.width(32)) multiplexer_8 (
    .in0(multiplier_1_cout), .in1(divider_1_rem), .out(multiplexer_8_out), .sel(Control[0]));
  Multiplexer #(.width(32)) multiplexer_9 (
    .in0(multiplexer_4_out), .in1(multiplexer_5_out), .out(multiplexer_9_out), .sel(Control[1]));
  Multiplexer #(.width(32)) multiplexer_10 (
    .in1(multiplexer_6_out), .out(multiplexer_10_out), .sel(Control[0]));  // open: in0
  Multiplexer #(.width(32)) multiplexer_11 (
    .in0(multiplier_1_out), .in1(divider_1_out), .out(multiplexer_11_out), .sel(Control[0]));
  Clock clock_1 (.out(clock_1_out));
  Multiplexer #(.width(32)) multiplexer_12 (
    .in0(multiplexer_9_out), .out(multiplexer_12_out), .sel(Control[2]));  // open: in1
  Register #(.width(32)) HI (.D(multiplexer_11_out), .en(Control[3]), .clk(clock_1_out), .Q(HI_q));  // open: clr
  Register #(.width(32)) LO (.D(multiplexer_8_out), .en(Control[3]), .clk(clock_1_out), .Q(LO_q));  // open: clr
  Multiplexer #(.width(32)) multiplexer_13 (
    .in1(multiplexer_10_out), .out(multiplexer_13_out), .sel(Control[1]));  // open: in0
  Multiplexer #(.width(32)) multiplexer_14 (.in0(HI_q), .in1(LO_q), .out(multiplexer_14_out), .sel(Control[0]));
  Multiplexer #(.width(32)) multiplexer_15 (
    .in0(multiplexer_14_out), .out(multiplexer_15_out), .sel(Control[1]));  // open: in1
  Multiplexer #(.width(32)) multiplexer_16 (
    .in0(multiplexer_15_out), .in1(multiplexer_13_out), .out(multiplexer_16_out), .sel(Control[1]));
  Multiplexer #(.width(32)) multiplexer_17 (
    .in0(multiplexer_12_out), .out(multiplexer_17_out), .sel(Control[3]));  // open: in1
  Multiplexer #(.width(32)) multiplexer_18 (
    .in0(multiplexer_17_out), .in1(multiplexer_16_out), .out(out_4), .sel(Control[2]));
endmodule

module MemoryController (
  input  [15:0] AddressFromBus,
  input  WriteEnableFromBus,
  input  [31:0] DataFromBus,
  input  [31:0] DataFromMem,
  output [15:0] AddressToMem,
  output WriteEnableToMem,
  output WriteToBus,
  output [31:0] DataToMem,
  output [31:0] DataToBus
);

  wire comparator_1_lt;

  // Probe on AddressFromBus
  // Probe on 16'hff80
  Comparator #(.mode("unsigned"), .width(16)) comparator_1 (
    .a(AddressFromBus), .b(16'hff80), .lt(comparator_1_lt));  // open: gt, eq
  and and_1 (WriteEnableToMem, comparator_1_lt, WriteEnableFromBus);
  and and_2 (WriteToBus, comparator_1_lt, ~WriteEnableFromBus);  // AND_Gate
  Shifter #(.shift("lr"), .width(16)) shifter_1 (.in(AddressFromBus), .\dist (4'b0010), .out(AddressToMem));

  assign DataToBus = DataFromMem;
  assign DataToMem = DataFromBus;
endmodule

module KeyboardController (
  input  [31:0] DataFromBus,
  input  [15:0] AddressFromBus,
  input  WriteEnableFromBus,
  input  KeyboardStatus,
  input  [6:0] KeyboardData,
  output KeyboardRead,
  output WriteToBus,
  output [31:0] DataToBus
);

  wire and_1_out, and_3_out, comparator_1_eq, comparator_2_eq, multiplexer_1_out, or_1_out;
  wire [6:0] multiplexer_2_out;

  Comparator #(.width(16)) comparator_1 (.a(AddressFromBus), .b(16'hff80), .eq(comparator_1_eq));  // open: gt, lt
  Comparator #(.width(16)) comparator_2 (.a(AddressFromBus), .b(16'hff84), .eq(comparator_2_eq));  // open: gt, lt
  Multiplexer multiplexer_1 (.in1(KeyboardStatus), .out(multiplexer_1_out), .sel(and_1_out));  // open: in0
  Multiplexer #(.width(7)) multiplexer_2 (.in1(KeyboardData), .out(multiplexer_2_out), .sel(and_3_out));  // open: in0
  or or_1 (or_1_out, comparator_1_eq, comparator_2_eq);
  and and_1 (and_1_out, ~WriteEnableFromBus, comparator_1_eq);  // AND_Gate
  and and_2 (KeyboardRead, WriteEnableFromBus, comparator_1_eq);
  and and_3 (and_3_out, ~WriteEnableFromBus, comparator_2_eq);  // AND_Gate
  assign DataToBus = {{31{multiplexer_1_out}}, multiplexer_1_out};  // Bit_Extender bit_extender_1
  assign DataToBus = {{25{multiplexer_2_out[6]}}, multiplexer_2_out};  // Bit_Extender bit_extender_2
  and and_4 (WriteToBus, ~WriteEnableFromBus, or_1_out);  // AND_Gate
endmodule

module RGBController (
  input  [15:0] AddressIn,
  input  WriteEnable,
  input  [31:0] DataBusIn,
  output [6:0] RGBX,
  output [6:0] RGBY,
  output [23:0] RGBColor,
  output RGBWrite
);

  wire and_1_out, and_2_out, and_3_out, clock_1_out, comparator_1_eq, comparator_2_eq, comparator_3_eq,
       comparator_4_eq;
  wire [31:0] register_1_q, register_2_q, register_3_q;

  Clock clock_1 (.out(clock_1_out));
  Comparator #(.mode("unsigned"), .width(16)) comparator_1 (
    .a(AddressIn), .b(16'hff90), .eq(comparator_1_eq));  // open: gt, lt
  Comparator #(.mode("unsigned"), .width(16)) comparator_2 (
    .a(AddressIn), .b(16'hff94), .eq(comparator_2_eq));  // open: gt, lt
  Comparator #(.mode("unsigned"), .width(16)) comparator_3 (
    .a(AddressIn), .b(16'hff98), .eq(comparator_3_eq));  // open: gt, lt
  Comparator #(.mode("unsigned"), .width(16)) comparator_4 (
    .a(AddressIn), .b(16'hff9c), .eq(comparator_4_eq));  // open: gt, lt
  and and_1 (and_1_out, WriteEnable, comparator_1_eq);
  and and_2 (and_2_out, WriteEnable, comparator_2_eq);
  and and_3 (and_3_out, WriteEnable, comparator_3_eq);
  and and_4 (RGBWrite, WriteEnable, comparator_4_eq);
  Register #(.width(32)) register_1 (.D(DataBusIn), .en(and_1_out), .clk(clock_1_out), .Q(register_1_q));  // open: clr
  Register #(.width(32)) register_2 (.D(DataBusIn), .en(and_2_out), .clk(clock_1_out), .Q(register_2_q));  // open: clr
  Register #(.width(32)) register_3 (.D(DataBusIn), .en(and_3_out), .clk(clock_1_out), .Q(register_3_q));  // open: clr
  Bit_Extender #(.in_width(32), .out_width(7), .\type ("zero")) bit_extender_1 (.in(register_1_q), .out(RGBX));
  Bit_Extender #(.in_width(32), .out_width(7), .\type ("zero")) bit_extender_2 (.in(register_2_q), .out(RGBY));
  Bit_Extender #(.in_width(32), .out_width(24), .\type ("zero")) bit_extender_3 (.in(register_3_q), .out(RGBColor));
endmodule

module Computer (
);

  wire clock_1_out, clock_2_out, clock_3_out, cpu_1_buswriteenable, joystick_control_1_joystick_we,
       keyb_1_keyboardread, keyb_1_writetobus, keyboard_1_avail, memorycontroller_1_writeenabletomem,
       memorycontroller_1_writetobus, rgb_video_1_p1, rgb_video_1_p2, sound_control_1_we,
       terminal_1_terminal_we;
  wire [3:0] undriven, undriven_2;
  wire [6:0] keyboard_1_data, rgb_video_1_p3, rgb_video_1_p4, sound_control_1_volume, terminal_1_databus_out;
  wire [13:0] sound_control_1_frequency;
  wire [15:0] cpu_1_addresstobus, memorycontroller_1_addresstomem;
  wire [23:0] rgb_video_1_p5;
  wire [31:0] controlled_buffer_1_out, cpu_1_datatobus, joystick_control_1_databus_out, keyb_1_datatobus,
       memorycontroller_1_datatobus, memorycontroller_1_datatomem, ram_1_dout;

  RAM #(.addrWidth(16), .dataWidth(32), .enables("line")) ram_1 (
    .addr(memorycontroller_1_addresstomem), .we(memorycontroller_1_writeenabletomem), .clk(clock_1_out),
    .din(memorycontroller_1_datatomem), .dout(ram_1_dout));
  Clock clock_1 (.out(clock_1_out));
  // Probe on ram_1_dout
  Clock clock_2 (.out(clock_2_out));
  Clock clock_3 (.out(clock_3_out));
  Keyboard keyboard_1 (
    .clk(clock_3_out), .re(keyb_1_keyboardread), .avail(keyboard_1_avail), .data(keyboard_1_data));  // open: clr
  TTY tty_1 (.data(terminal_1_databus_out), .clk(clock_2_out), .we(terminal_1_terminal_we));  // open: clr
  MemoryController memorycontroller_1 (
    .AddressFromBus(cpu_1_addresstobus), .WriteEnableFromBus(cpu_1_buswriteenable),
    .DataFromBus(controlled_buffer_1_out), .DataFromMem(ram_1_dout),
    .AddressToMem(memorycontroller_1_addresstomem), .WriteEnableToMem(memorycontroller_1_writeenabletomem),
    .WriteToBus(memorycontroller_1_writetobus), .DataToMem(memorycontroller_1_datatomem),
    .DataToBus(memorycontroller_1_datatobus));
  CPU cpu_1 (
    .DataFromBus(controlled_buffer_1_out), .BusWriteEnable(cpu_1_buswriteenable),
    .AddressToBus(cpu_1_addresstobus), .DataToBus(cpu_1_datatobus));
  Terminal terminal_1 (
    .DataBus_In(controlled_buffer_1_out), .Address(cpu_1_addresstobus), .DateBus_WE(cpu_1_buswriteenable),
    .DataBus_Out(terminal_1_databus_out), .Terminal_WE(terminal_1_terminal_we));
  // Probe on memorycontroller_1_datatobus
  assign controlled_buffer_1_out = memorycontroller_1_writetobus ? memorycontroller_1_datatobus : 32'bz;  // Controlled_Buffer controlled_buffer_1
  assign controlled_buffer_1_out = cpu_1_buswriteenable ? cpu_1_datatobus : 32'bz;  // Controlled_Buffer controlled_buffer_2
  // Probe on memorycontroller_1_writetobus
  // Probe on cpu_1_buswriteenable
  // Probe on keyb_1_writetobus
  KeyB keyb_1 (
    .WriteEnableFromBus(cpu_1_buswriteenable), .AddressFromBus(cpu_1_addresstobus),
    .DataFromBus(controlled_buffer_1_out), .KeyboardStatus(keyboard_1_avail), .KeyboardData(keyboard_1_data),
    .KeyboardRead(keyb_1_keyboardread), .WriteToBus(keyb_1_writetobus), .DataToBus(keyb_1_datatobus));
  assign controlled_buffer_1_out = keyb_1_writetobus ? keyb_1_datatobus : 32'bz;  // Controlled_Buffer controlled_buffer_3
  // RGB_Video rgb_video_1: pin names not known; wires that end beside it: rgb_video_1_p1, rgb_video_1_p2, rgb_video_1_p3, rgb_video_1_p4, rgb_video_1_p5
  Clock clock_4 (.out(rgb_video_1_p1));
  // Probe on cpu_1_buswriteenable
  // Probe on cpu_1_addresstobus
  // Probe on controlled_buffer_1_out
  Joystick joystick_1 ();  // open: x, y
  assign controlled_buffer_1_out = joystick_control_1_joystick_we ? joystick_control_1_databus_out : 32'bz;  // Controlled_Buffer controlled_buffer_4
  JoyStick_Control joystick_control_1 (
    .X(undriven_2), .Y(undriven), .AddressIn(cpu_1_addresstobus),
    .DataBus_Out(joystick_control_1_databus_out), .JoyStick_WE(joystick_control_1_joystick_we));
  RGBController rgbcontroller_1 (
    .AddressIn(cpu_1_addresstobus), .WriteEnable(cpu_1_buswriteenable), .DataBusIn(controlled_buffer_1_out),
    .RGBX(rgb_video_1_p3), .RGBY(rgb_video_1_p4), .RGBColor(rgb_video_1_p5), .RGBWrite(rgb_video_1_p2));
  Sound_Control sound_control_1 (
    .DataBus_In(controlled_buffer_1_out), .Address(cpu_1_addresstobus), .DateBus_WE(cpu_1_buswriteenable),
    .Frequency(sound_control_1_frequency), .WE(sound_control_1_we), .Volume(sound_control_1_volume));
  // Probe on rgb_video_1_p3
  // Probe on rgb_video_1_p4
  // Probe on rgb_video_1_p5
  // Probe on rgb_video_1_p2
  // Buzzer buzzer_1: pin names not known; wires that end beside it: sound_control_1_frequency, sound_control_1_we, sound_control_1_volume

  // Notes on the sheet:
  //   works
  //   Write_enable
  //   Address
  //   Data
  //   is not utilized
  //   works
endmodule

module KeyB (
  input  WriteEnableFromBus,
  input  [15:0] AddressFromBus,
  input  [31:0] DataFromBus,
  input  KeyboardStatus,
  input  [6:0] KeyboardData,
  output KeyboardRead,
  output WriteToBus,
  output [31:0] DataToBus
);

  wire and_1_out, and_2_out, comparator_1_eq, comparator_2_eq, not_1_out, or_1_out;
  wire [31:0] bit_extender_1_out, bit_extender_2_out, multiplexer_1_out;

  assign bit_extender_1_out = {{31{1'b0}}, KeyboardStatus};  // Bit_Extender bit_extender_1
  Comparator #(.mode("unsigned"), .width(16)) comparator_1 (
    .a(AddressFromBus), .b(16'hff80), .eq(comparator_1_eq));  // open: gt, lt
  Comparator #(.mode("unsigned"), .width(16)) comparator_2 (
    .a(AddressFromBus), .b(16'hff84), .eq(comparator_2_eq));  // open: gt, lt
  assign bit_extender_2_out = {{25{1'b0}}, KeyboardData};  // Bit_Extender bit_extender_2
  not not_1 (not_1_out, WriteEnableFromBus);
  and and_1 (and_1_out, comparator_1_eq, not_1_out);
  Multiplexer #(.width(32)) multiplexer_1 (
    .in0(DataFromBus), .in1(bit_extender_1_out), .out(multiplexer_1_out), .sel(and_1_out));
  and and_2 (and_2_out, comparator_2_eq, not_1_out);
  Multiplexer #(.width(32)) multiplexer_2 (
    .in0(multiplexer_1_out), .in1(bit_extender_2_out), .out(DataToBus), .sel(and_2_out));
  and and_3 (KeyboardRead, WriteEnableFromBus, comparator_1_eq);
  or or_1 (or_1_out, comparator_1_eq, comparator_2_eq);
  and and_4 (WriteToBus, or_1_out, not_1_out);
  // Probe on WriteToBus
  // Probe on DataToBus
  // Probe on and_2_out
endmodule

module Sound_Control (
  input  [31:0] DataBus_In,
  input  [15:0] Address,
  input  DateBus_WE,
  output [13:0] Frequency,
  output WE,
  output [6:0] Volume
);

  wire and_1_out, and_3_out, comparator_1_eq, comparator_2_eq, comparator_3_eq;
  wire [31:0] register_1_q, register_2_q;

  Comparator #(.mode("unsigned"), .width(16)) comparator_1 (
    .a(Address), .b(16'hffa4), .eq(comparator_1_eq));  // open: gt, lt
  Comparator #(.mode("unsigned"), .width(16)) comparator_2 (
    .a(Address), .b(16'hffa8), .eq(comparator_2_eq));  // open: gt, lt
  Comparator #(.mode("unsigned"), .width(16)) comparator_3 (
    .a(Address), .b(16'hffac), .eq(comparator_3_eq));  // open: gt, lt
  and and_1 (and_1_out, comparator_1_eq, DateBus_WE);
  and and_2 (WE, comparator_2_eq, DateBus_WE);
  and and_3 (and_3_out, comparator_3_eq, DateBus_WE);
  Register #(.width(32)) register_1 (.D(DataBus_In), .en(and_1_out), .Q(register_1_q));  // open: clk, clr
  Register #(.width(32)) register_2 (.D(DataBus_In), .en(and_3_out), .Q(register_2_q));  // open: clk, clr
  Bit_Extender #(.in_width(32), .out_width(14), .\type ("zero")) bit_extender_1 (.in(register_1_q), .out(Frequency));
  Bit_Extender #(.in_width(32), .out_width(7), .\type ("zero")) bit_extender_2 (.in(register_2_q), .out(Volume));
endmodule

module Terminal (
  input  [31:0] DataBus_In,
  input  [15:0] Address,
  input  DateBus_WE,
  output [6:0] DataBus_Out,
  output Terminal_WE
);

  wire comparator_1_eq;

  Comparator #(.width(16)) comparator_1 (.a(Address), .b(16'hffa0), .eq(comparator_1_eq));  // open: gt, lt
  Bit_Extender #(.in_width(32), .out_width(7)) bit_extender_1 (.in(DataBus_In), .out(DataBus_Out));
  and and_1 (Terminal_WE, comparator_1_eq, DateBus_WE);
endmodule

module JoyStick_Control (
  input  [3:0] X,
  input  [3:0] Y,
  input  [15:0] AddressIn,
  output [31:0] DataBus_Out,
  output JoyStick_WE
);

  wire comparator_1_eq, comparator_2_eq;
  wire [3:0] multiplexer_1_out;

  Comparator #(.mode("unsigned"), .width(16)) comparator_1 (
    .a(AddressIn), .b(16'hffac), .eq(comparator_1_eq));  // open: gt, lt
  Comparator #(.mode("unsigned"), .width(16)) comparator_2 (
    .a(AddressIn), .b(16'hffb0), .eq(comparator_2_eq));  // open: gt, lt
  Multiplexer #(.width(4)) multiplexer_1 (.in0(X), .in1(Y), .out(multiplexer_1_out), .sel(comparator_2_eq));
  assign DataBus_Out = {{28{multiplexer_1_out[3]}}, multiplexer_1_out};  // Bit_Extender bit_extender_1
  or or_1 (JoyStick_WE, comparator_1_eq, comparator_2_eq);
endmodule
